# Fritzing sketch LoRa-433-1 (saved by Fritzing 0.9.3b)
circuit board: 16.2072cm x 6.53238cm
breadboards: 1

parts:
  RFM95W = Adafruit RFM9x LoRa Radio [part_number="Adafruit #3072 and #3073"]
  ATMEGA2560 = Arduino Mega 2560 (Rev3)

nets:
  VIN: RFM95W.VIN, RFM95W.EN, ATMEGA2560.5V
  GND: RFM95W.GND, ATMEGA2560.GND
  N1: RFM95W.DIO0, ATMEGA2560.D3_PWM
  N2: RFM95W.SCK, ATMEGA2560.D52
  N3: RFM95W.MISO, ATMEGA2560.D50
  N4: RFM95W.MOSI, ATMEGA2560.D51
  N5: RFM95W.CS, ATMEGA2560.D4_PWM
  N6: RFM95W.RST, ATMEGA2560.D2_PWM

custom parts:
  Adafruit RFM9x LoRa Radio: Sending data over long distances is like magic, and now you can be a magician with this range of powerful and easy-to-use radio modules. Sure, sometimes you want to talk to a computer (a good time to use WiFi) or perhaps communicate with a Phone (choose Bluetooth Low Energy!) but what if you want to send data very far? Most WiFi, Bluetooth, Zigbee and other wireless chipsets use 2.4GHz, which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
