# Fritzing sketch LoRa_client (saved by Fritzing 0.9.3b)
breadboards: 1

parts:
  uno = Arduino Uno (Rev3)
  R1 = Resistor [tolerance=±5% resistance=220 package="2010 [SMD]"]
  LED1 = smd LED [color="Red (633nm)" package="0603 [SMD]"]
  Part1 = Adafruit RFM69HCW Transceiver Radio [part_number="Adafruit #3070 and #3071"]

nets:
  N1: uno.D10_PWM/SS, Part1.CS
  N2: uno.D11_PWM/MOSI, Part1.MOSI
  N3: uno.D12/MISO, Part1.MISO
  N4: uno.D13/SCK, Part1.SCK
  GND: uno.GND, LED1.cathode, Part1.GND
  N5: uno.D2, Part1.RST
  N6: uno.D3_PWM, Part1.DIO0
  N7: uno.D7, R1.Pin_0
  5V: uno.5V, Part1.VIN, Part1.EN
  N8: R1.Pin_1, LED1.anode

custom parts:
  Adafruit RFM69HCW Transceiver Radio: Sending data over long distances is like magic, and now you can be a magician with this range of powerful and easy-to-use radio modules. Sure, sometimes you want to talk to a computer (a good time to use WiFi) or perhaps communicate with a Phone (choose Bluetooth Low Energy!) but what if you want to send data very far? Most WiFi, Bluetooth, Zigbee and other wireless chipsets use 2.4GHz, which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
